# Fritzing sketch stm32-i2s-beep-detection (saved by Fritzing 0.9.10b)
breadboards: 1

parts:
  Part1 = Adafruit HUZZAH32 ESP32 Feather [part_number="Adafruit #3405"]
  Part2 = Adafruit I2S Mic - SPH0645 [part_number="Adafruit #3421"]

nets:
  N1: Part1.A1_DAC1, Part2.WS
  N2: Part1.A0_DAC2, Part2.BCLK
  GND: Part1.GND, Part2.GND
  3.3V: Part1.3.3V, Part2.VDD
  N3: Part1.SCL, Part2.DATA

custom parts:
  Adafruit I2S Mic - SPH0645: For many microcontrollers, adding audio input is easy with one of our analog microphone breakouts. But as you get to bigger and better microcontrollers and microcomputers, you'll find that you don't always have an analog input, or maybe you want to avoid the noise that can seep in with an analog mic system. Once you get past 8-bit micros, you will often find an I2S peripheral, that can take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
